# Fritzing sketch arduino_dynamixel_ax12 (saved by Fritzing 0.9.3b)
breadboards: 1

parts:
  Part1 = Arduino Uno (Rev3) - ICSP
  servo4 = Dagu DGServo 9g header connector (female) [package=THT]
  servo5 = Dagu DGServo 9g header connector (female) [package=THT]
  servo6 = Dagu DGServo 9g header connector (female) [package=THT]
  9-12V = Power Jack [package=power_jack_smd]
  R1 = Resistor [tolerance=±5% resistance=10k package="0805 [SMD]"]
  U9 = POT [package=pot_alpha_rv16af-20]
  USBTTL2 = USB TTL Serial Cable
  9-12V_2 = DC Power [voltage=5]
  74LS241 = IC, DIP package, 20 pins [chip_label=74LS241]

nets:
  N1: Part1.A4/SDA, U9.S
  5V: Part1.5V, R1.Pin_1, U9.E, USBTTL2.5V, 74LS241.pin20
  GND: Part1.GND, servo4.gnd, servo5.gnd, servo6.gnd, 9-12V.GNDBREAK, U9.A, USBTTL2.GND, 74LS241.pin10
  N2: Part1.D8, USBTTL2.TX
  N3: Part1.D9_PWM, USBTTL2.RX
  N4: Part1.D0/RX, 74LS241.pin18
  N5: Part1.D1/TX, 74LS241.pin17
  N6: Part1.D2, 74LS241.pin1, 74LS241.pin19
  VCC: servo4.Vcc, servo5.Vcc, servo6.Vcc
  N7: servo4.pulse, servo5.pulse, servo6.pulse, R1.Pin_0, 74LS241.pin2, 74LS241.pin3
  N8: 9-12V.PWR, 9-12V_2.V+
  N9: 9-12V.GND, 9-12V_2.V-
